# Fritzing sketch NodeMCUx2_wOLEDs (saved by Fritzing 0.9.3b)
breadboards: 1

parts:
  U1 = NodeMCU V1.0
  Squix1 = OLED 0.96" 128x64 I2C SSD1306
  U2 = NodeMCU V1.0
  Squix2 = OLED 0.96" 128x64 I2C SSD1306

nets:
  N1: U1.D1, Squix1.SCL
  N2: U1.D2, Squix1.SCA
  3V3: U1.3V3, Squix1.VCC
  GND: U1.GND, Squix1.GND, U2.GND, Squix2.GND
  VIN: U1.Vin, U2.Vin
  N3: U2.D1, Squix2.SCL
  N4: U2.D2, Squix2.SCA
  3V3_2: U2.3V3, Squix2.VCC

custom parts:
  NodeMCU V1.0: ESP8266 based NodeMCU
